# Fritzing sketch cpap_ventilator_schema (saved by Fritzing 0.9.4)
circuit board: 8.46667cm x 5.64444cm

parts:
  R1 = Rotary Potentiometer (Large) [maximum_resistance=100kΩ package=THT]
  Bauteil1 = Arduino Uno (Rev3) - ICSP
  LED1 = smd LED [color="Yellow (595nm)" package="0805 [SMD]"]
  LED3 = smd LED [color="Green (565nm)" package="0805 [SMD]"]
  U1 = SWITCH_SPDT [package=kps-1290]
  R2 = Resistor [tolerance=±5% resistance=220 package="1206 [SMD]"]
  R3 = Resistor [tolerance=±5% resistance=220 package="1206 [SMD]"]
  R4 = Resistor [tolerance=±5% resistance=220 package="1206 [SMD]"]
  LED4 = smd LED [color="Infrared (880nm)" package="0805 [SMD]"]
  Q1 = TRANSISTOR_NPN [package=to-92-ammo]
  J2 = Basic Servo
  LED6 = smd LED [color="Red (633nm)" package="0805 [SMD]"]
  R6 = Resistor [tolerance=±5% resistance=220 package="1206 [SMD]"]
  S1 = Momentary Switch [package=ksa_sealed_tac_switch]
  J3 = Piezo Speaker
  LCM1602_IIC1 = LCM1602 IIC [part_number="LCM1602 IIC" chip_label="LCM1602 IIC" package="DIP (Dual Inline) [THT]"]
  LCD1 = LCD screen

nets (from the breadboard view):
  GND: R1.leg1, Bauteil1.GND, U1.P, R2.Pin_1, R3.Pin_1, R4.Pin_1, Q1.E, J2.gnd, R6.Pin_1, S1.2, J3.pin2, LCM1602_IIC1.GND
  N1: R1.wiper, Bauteil1.A0
  VCC: R1.leg2, Bauteil1.5V, LED4.anode, Q1.C, J2.vcc, LCM1602_IIC1.VCC
  N2: Bauteil1.D11_PWM/MOSI, J2.pulse
  N3: Bauteil1.D12/MISO, Q1.B
  N4: Bauteil1.A4/SDA, LCM1602_IIC1.SDA
  N5: Bauteil1.A5/SCL, LCM1602_IIC1.SCL
  N6: Bauteil1.D2, U1.S
  N7: Bauteil1.D3_PWM, S1.3
  N8: Bauteil1.D4, J3.pin1
  N9: Bauteil1.D5_PWM, LED3.anode
  N10: Bauteil1.D6_PWM, LED1.anode
  N11: Bauteil1.D7, LED6.anode
  N12: LED1.cathode, R4.Pin_0
  N13: LED3.cathode, R3.Pin_0
  N14: R2.Pin_0, LED6.cathode
  VSS: LCM1602_IIC1.VSS, LCD1.VSS
  VDD: LCM1602_IIC1.VDD, LCD1.VDD
  N15: LCM1602_IIC1.V0, LCD1.V0
  N16: LCM1602_IIC1.RS, LCD1.RS
  N17: LCM1602_IIC1.RW, LCD1.R/W
  N18: LCM1602_IIC1.E, LCD1.E
  N19: LCM1602_IIC1.D0, LCD1.DB0
  N20: LCM1602_IIC1.D1, LCD1.DB1
  N21: LCM1602_IIC1.D2, LCD1.DB2
  N22: LCM1602_IIC1.D3, LCD1.DB3
  N23: LCM1602_IIC1.D4, LCD1.DB4
  N24: LCM1602_IIC1.D5, LCD1.DB5
  N25: LCM1602_IIC1.D6, LCD1.DB6
  N26: LCM1602_IIC1.D7, LCD1.DB7
  N27: LCM1602_IIC1.A, LCD1.LED+
  N28: LCM1602_IIC1.K, LCD1.LED-
  N29: LCM1602_IIC1.LED_A, LCM1602_IIC1.LED_B

custom parts:
  LCM1602 IIC: I2C-Module to use a 1602 or 2004 LCD on with the wire.h libory Serial LCD Modul
